# Fritzing sketch PCB ESP32 PC PowerManager (saved by Fritzing 1.0.6)
circuit board: 3.80758cm x 3.45326cm
breadboards: 1

parts:
  IO = female pin header, 4 pins [form="♀ (female)"]
  J1 = female pin header, 7 pins [form="♀ (female)"]
  J2 = female pin header, 7 pins [form="♀ (female)"]
  220Ω = Resistor [tolerance=±5% resistance=220 power=0.25W package=THT]
  10kΩ = Resistor [tolerance=±5% power=0.25W resistance=10k package=THT]
  Power = female pin header, 2 pins [form="♀ (female)"]
  DHT = female pin header, 3 pins [form="♀ (female)"]
  NVY17-3 = Optocoupler [package=THT]
  LED1 = LED - 5mm [color="Red (633nm)" current=0.030A package="5 mm [THT]"]

nets:
  N1: IO.pin1, NVY17-3.Pin_4
  N2: IO.pin2, NVY17-3.Pin_5
  N3: IO.pin3, J1.pin2, 10kΩ.Pin_1
  N4: IO.pin4, J2.pin2, Power.pin2, DHT.pin1, NVY17-3.Pin_2, LED1.anode
  N5: J1.pin3, DHT.pin2
  N6: J1.pin4, LED1.cathode
  N7: J2.pin1, Power.pin1
  N8: J2.pin3, 10kΩ.Pin_0, DHT.pin3
  N9: J2.pin7, 220Ω.Pin_0
  N10: 220Ω.Pin_1, NVY17-3.Pin_1

notes:
  toPC
  toSwitch
  Designed by The12Forest
  XIAO ESP32 C3
  5V
  GND
  3V3
  D10
  D09
  D08
  D07 to PC
  D06
  D05
  D04
  D03
  D02
  Button D01
  D00
  2026 Sep. 19
  LED
  3v3
  Data
